# Fritzing sketch LED_bike_remote (saved by Fritzing 0.9.10b)
breadboards: 1

parts:
  S1 = Pushbutton [package="[THT]"]
  Part2 = Arduino Nano (Rev3.0) (ICSP)
  LED1 = smd LED [color="Yellow (585nm)" package="0805 [SMD]"]
  R2 = Resistor [tolerance=±5% resistance=220 power=0.25 package=THT]
  S2 = Pushbutton [package="[THT]"]
  R3 = Resistor [tolerance=±5% resistance=100 power=0.25 package=THT]
  R4 = Resistor [tolerance=±5% resistance=220 power=0.25 package=THT]
  LED2 = smd LED [color="Yellow (585nm)" package="0805 [SMD]"]
  R1 = Resistor [tolerance=±5% resistance=100 power=0.25 package=THT]
  C1 = Capacitor Polarized [package=panasonic_c]
  Part4 = Bluetooth HC-05 Macho
  Part5 = InvenSense MPU6050
  S3 = Toggle Switch [package=THT]
  VCC1 = 4 x AAA Battery Mount

nets:
  N1: S1.Pin_1, S1.Pin_2, Part2.D4, R1.Pin_0
  VCC: S1.Pin_3, S1.Pin_4, Part2.VIN, S2.Pin_3, S2.Pin_4, C1.+, Part4.VCC, Part5.VCC, VCC1.+
  N2: Part2.D1/TX, Part4.RXD
  N3: Part2.D0/RX, Part4.TXD
  N4: Part2.D3, S2.Pin_1, S2.Pin_2, R3.Pin_0
  N5: Part2.D7, LED1.anode
  N6: Part2.D8, LED2.anode
  N7: Part2.D9, S3.COM
  N8: Part2.A5, Part5.SCL
  N9: Part2.A4, Part5.SDA
  N10: LED1.cathode, R2.Pin_0
  GND: R2.Pin_1, R3.Pin_1, R4.Pin_1, R1.Pin_1, C1.-, Part4.GND, Part5.GND, S3.L1, VCC1.-
  N11: R4.Pin_0, LED2.cathode
