# Fritzing sketch LED_bike_vest (saved by Fritzing 0.9.10b)
breadboards: 1

parts:
  Part2 = Arduino Nano (Rev3.0) (ICSP)
  C1 = Capacitor Polarized [package=panasonic_c]
  Part4 = Bluetooth HC-05 Macho
  R6 = Resistor [tolerance=±5% resistance=100 power=0.25 package=THT]
  R7 = Resistor [tolerance=±5% resistance=100 power=0.25 package=THT]
  R8 = Resistor [tolerance=±5% resistance=100 power=0.25 package=THT]
  U3 = WS2812 RGB LED strip
  U4 = WS2812 RGB LED strip
  U5 = WS2812 RGB LED strip
  VCC2 = 4 x AAA Battery Mount

nets:
  N1: Part2.D1/TX, Part4.RXD
  N2: Part2.D0/RX, Part4.TXD
  N3: Part2.D4, R6.Pin_1
  N4: Part2.D5, R7.Pin_1
  N5: Part2.D6, R8.Pin_1
  VCC: Part2.5V, C1.+, Part4.VCC, U3.VCC, U4.VCC, U5.VCC, VCC2.+
  GND: C1.-, Part4.GND, U3.GND, U4.GND, U5.GND, VCC2.-
  N6: R6.Pin_0, U5.DIN
  N7: R7.Pin_0, U4.DIN
  N8: R8.Pin_0, U3.DIN

custom parts:
  WS2812 RGB LED strip: WS2812 strip
